# Fritzing sketch CS2710CirclePong (saved by Fritzing 0.9.3b)
breadboards: 3

parts:
  Game_Mega = Arduino Mega 2560 (Rev3)
  Display_Mega = Arduino Mega 2560 (Rev3)
  Game_Display = LBT2088AH
  Game_Controller = Thumb Joystick
  Start_Button = Pushbutton [package="[SMD]"]
  Start_Pull-Down_Resistor = Resistor [tolerance=±5% resistance=220 package=THT]
  Score_Display = LCD screen
  Passive_Buzzer = Buzzer 12mm [package=buzzer-12mm-ns]
  Speaker = Loudspeaker
  LCM1602_IIC2 = LCM1602 IIC [part_number="LCM1602 IIC" chip_label="LCM1602 IIC" package="DIP (Dual Inline) [THT]"]
  Serial_MP3_Player_Header = Header 6 [package=em406]
  Quiet_Button = Pushbutton [package="[SMD]"]
  Quick_Reset_Pull-Up_Resistor = Resistor [tolerance=±5% resistance=220 package=THT]
  Quiet_Button_Pull-Down_Resistor = Resistor [tolerance=±5% resistance=220 package=THT]

nets:
  N1: Game_Mega.A1, Game_Controller.HORZ
  N2: Game_Mega.A2, Game_Controller.VERT
  N3: Game_Mega.D21/SCL, LCM1602_IIC2.SCL
  N4: Game_Mega.D20/SDA, Game_Mega.SDA, LCM1602_IIC2.SDA
  N5: Game_Mega.D19/RX1, Serial_MP3_Player_Header.6
  N6: Game_Mega.D18/TX1, Serial_MP3_Player_Header.5
  GND: Game_Mega.GND, Display_Mega.GND, Game_Controller.GND, Start_Pull-Down_Resistor.Pin_1, Passive_Buzzer.2, LCM1602_IIC2.GND, Serial_MP3_Player_Header.3, Quiet_Button_Pull-Down_Resistor.Pin_0
  N7: Game_Mega.D9_PWM, Passive_Buzzer.1
  N8: Game_Mega.D3_PWM, Quiet_Button.Pin_3, Quiet_Button.Pin_4, Quiet_Button_Pull-Down_Resistor.Pin_1
  N9: Game_Mega.D5_PWM, Display_Mega.D5_PWM
  VCC: Game_Mega.5V, Game_Controller.VCC, Start_Button.Pin_1, Start_Button.Pin_2, LCM1602_IIC2.VCC, Serial_MP3_Player_Header.4, Quiet_Button.Pin_1, Quiet_Button.Pin_2, Quick_Reset_Pull-Up_Resistor.Pin_1
  N10: Game_Mega.D22, Display_Mega.D22
  N11: Game_Mega.D23, Display_Mega.D23
  N12: Game_Mega.D24, Display_Mega.D24
  N13: Game_Mega.D25, Display_Mega.D25
  N14: Game_Mega.D26, Display_Mega.D26
  N15: Game_Mega.D27, Display_Mega.D27
  N16: Game_Mega.D28, Display_Mega.D28
  N17: Game_Mega.D29, Display_Mega.D29
  N18: Game_Mega.D30, Display_Mega.D30
  N19: Game_Mega.D31, Display_Mega.D31
  N20: Game_Mega.D33, Display_Mega.D33
  N21: Game_Mega.D52, Game_Controller.SEL, Quick_Reset_Pull-Up_Resistor.Pin_0
  N22: Game_Mega.D53, Start_Button.Pin_3, Start_Button.Pin_4, Start_Pull-Down_Resistor.Pin_0
  N23: Display_Mega.D38, Game_Display.pin_9
  N24: Display_Mega.D39, Game_Display.pin_8
  N25: Display_Mega.D40, Game_Display.pin_10
  N26: Display_Mega.D41, Game_Display.pin_7
  N27: Display_Mega.D42, Game_Display.pin_11
  N28: Display_Mega.D43, Game_Display.pin_6
  N29: Display_Mega.D44, Game_Display.pin_12
  N30: Display_Mega.D45, Game_Display.pin_5
  N31: Display_Mega.D46, Game_Display.pin_13
  N32: Display_Mega.D47, Game_Display.pin_4
  N33: Display_Mega.D48, Game_Display.pin_14
  N34: Display_Mega.D49, Game_Display.pin_3
  N35: Display_Mega.D50, Game_Display.pin_15
  N36: Display_Mega.D51, Game_Display.pin2
  N37: Display_Mega.D52, Game_Display.pin_16
  N38: Display_Mega.D53, Game_Display.pin1
  VSS: Score_Display.VSS, LCM1602_IIC2.VSS
  VDD: Score_Display.VDD, LCM1602_IIC2.VDD
  N39: Score_Display.V0, LCM1602_IIC2.V0
  N40: Score_Display.RS, LCM1602_IIC2.RS
  N41: Score_Display.R/W, LCM1602_IIC2.RW
  N42: Score_Display.E, LCM1602_IIC2.E
  N43: Score_Display.DB0, LCM1602_IIC2.D0
  N44: Score_Display.DB1, LCM1602_IIC2.D1
  N45: Score_Display.DB2, LCM1602_IIC2.D2
  N46: Score_Display.DB3, LCM1602_IIC2.D3
  N47: Score_Display.DB4, LCM1602_IIC2.D4
  N48: Score_Display.DB5, LCM1602_IIC2.D5
  N49: Score_Display.DB6, LCM1602_IIC2.D6
  N50: Score_Display.DB7, LCM1602_IIC2.D7
  N51: Score_Display.LED+, LCM1602_IIC2.A
  N52: Score_Display.LED-, LCM1602_IIC2.K
  N53: Speaker.pin1, Serial_MP3_Player_Header.2
  N54: Speaker.pin2, Serial_MP3_Player_Header.1

custom parts:
  LCM1602 IIC: I2C-Module to use a 1602 or 2004 LCD on with the wire.h libory Serial LCD Modul
